// Logisim project OISC_v4_1.circ as structural Verilog: 4 circuits, main circuit main
module main (
  input  in_1,
  input  in_2,
  output [2:0] out_3,
  output [7:0] out_4,
  output [7:0] out_5,
  output [7:0] out_6,
  output [2:0] out_7
);

  wire A_DAT_EN, ABC_REG_EN, and_1_out, and_2_out, B_DAT_EN, CLK, CNTR_EN, EXT, IO_1_EN, IO_2_EN, JMP_RDY,
       nA_B, nCNTR_REG, not_1_out, not_2_out, OFFSET_EN, RAM__IN_OUT, RAM_IN_STR, SUBLEQ_LOG;
  wire [4:0] OFFSET_REG;
  wire [7:0] A_DAT, A_REG, B_DAT, B_REG, C_REG, controlled_buffer_1_out, counter_1_q, IO_DATA_IN,
       IO_DATA_OUT, multiplexer_1_out, multiplexer_3_out, ram_1_data, RAM_ADDR, register_1_q;
  wire [7:7] or_1_out;

  and and_1 (and_1_out, SUBLEQ_LOG, JMP_RDY);
  Counter counter_1 (
    .load(and_1_out), .D(C_REG), .count(CNTR_EN), .Q(counter_1_q), .up(1'b1), .clk(CLK), .clr(in_2));  // open: carry
  Multiplexer #(.enable("false"), .width(8)) multiplexer_1 (
    .in0(A_REG), .in1(B_REG), .out(multiplexer_1_out), .sel(nA_B));
  Multiplexer #(.enable("false"), .width(8)) multiplexer_2 (
    .in0(counter_1_q), .in1(multiplexer_1_out), .out(RAM_ADDR), .sel(nCNTR_REG));
  FSM fsm_1 (
    .stage(out_7), .RAM_IN_STR(RAM_IN_STR), .RAM__IN_OUT(RAM__IN_OUT), .ABC_REG_EN(ABC_REG_EN),
    .A_DAT_EN(A_DAT_EN), .B_DAT_EN(B_DAT_EN), .nA_B(nA_B), .CNTR_EN(CNTR_EN), .nCNTR_REG(nCNTR_REG),
    .JMP_RDY(JMP_RDY), .CLK(CLK), .RST(in_2));
  assign controlled_buffer_1_out = EXT ? out_5 : 8'bz;  // Controlled_Buffer controlled_buffer_1
  or or_1 (or_1_out[7], RAM_ADDR[7], OFFSET_REG[0]);
  LED led_1 (.in(register_1_q[7]));
  LED led_2 (.in(register_1_q[6]));
  LED led_3 (.in(register_1_q[5]));
  Register register_1 (.D(controlled_buffer_1_out), .en(IO_1_EN), .Q(register_1_q), .clk(CLK), .clr(in_2));
  RAM #(.addrWidth(12), .databus("bidir")) ram_1 (
    .addr({OFFSET_REG[4:1], or_1_out[7], RAM_ADDR[6:0]}), .data(ram_1_data));  // open: we, oe, clk
  Clock clock_1 (.out(CLK));
  LED led_4 (.in(register_1_q[4]));
  LED led_5 (.in(register_1_q[3]));
  LED led_6 (.in(register_1_q[2]));
  LED led_7 (.in(register_1_q[1]));
  LED led_8 (.in(register_1_q[0]));
  // _7_Segment_Display 7_segment_display_1: pin names not known; wires that end beside it: register_1_q[7:4], register_1_q[3:0]
  // Hex_to_7_Segment_decoder hex_to_7_segment_decoder_1: pin names not known
  Register register_2 (.D(IO_DATA_OUT), .en(OFFSET_EN), .Q({out_3, OFFSET_REG}), .clk(CLK), .clr(in_2));
  SUBLEQ subleq_1 (.out_val(out_5), .leq_log(SUBLEQ_LOG), .in_1(B_DAT), .in_2(A_DAT));
  _7_Segment_Display u_7_segment_display_2 ();  // open: g, f, a, b, e, d, c, dp
  // Hex_to_7_Segment_decoder hex_to_7_segment_decoder_2: pin names not known
  // DipSwitch dipswitch_1: pin names not known; wires that end beside it: IO_DATA_IN[0], IO_DATA_IN[1], IO_DATA_IN[2], IO_DATA_IN[3], IO_DATA_IN[4], IO_DATA_IN[5], IO_DATA_IN[6], IO_DATA_IN[7]
  assign ram_1_data = not_2_out ? out_5 : 8'bz;  // Controlled_Buffer controlled_buffer_2
  assign out_4 = not_1_out ? ram_1_data : 8'bz;  // Controlled_Buffer controlled_buffer_3
  not not_1 (not_1_out, not_2_out);
  not not_2 (not_2_out, RAM__IN_OUT);
  and and_2 (and_2_out, EXT, A_DAT_EN);
  Multiplexer #(.enable("false"), .width(8)) multiplexer_3 (
    .in0(out_4), .in1(IO_DATA_IN), .out(multiplexer_3_out), .sel(and_2_out));
  PLA #(.in_width(8), .out_width(4), .\table ("11111111 1001 # io1\n11111110 1010 # io2\n11111101 1100 # bk1")) pla_1 (
    .in(RAM_ADDR), .out({EXT, OFFSET_EN, IO_2_EN, IO_1_EN}));
  Register register_3 (.D(out_4), .en(ABC_REG_EN), .Q(C_REG), .clk(CLK), .clr(in_2));
  Register register_4 (.D(C_REG), .en(ABC_REG_EN), .Q(B_REG), .clk(CLK), .clr(in_2));
  Register register_5 (.D(B_REG), .en(ABC_REG_EN), .Q(A_REG), .clk(CLK), .clr(in_2));
  Register register_6 (.D(multiplexer_3_out), .en(A_DAT_EN), .Q(A_DAT), .clk(CLK), .clr(in_2));
  Register register_7 (.D(multiplexer_3_out), .en(B_DAT_EN), .Q(B_DAT), .clk(CLK), .clr(in_2));

  assign out_6 = out_5;

  // Other names for the same wires on the sheet: REG_DATA[7:0] = out_4; RESET = in_2; SUBLEQ_RES[7:0] = out_5
endmodule

module SUBLEQ (
  input  [7:0] in_1,
  input  [7:0] in_2,
  output [7:0] out_val,
  output leq_log
);

  wire comparator_1_eq, comparator_1_lt;

  Subtractor subtractor_1 (.a(in_1), .b(in_2), .out(out_val));  // open: bin, bout
  Comparator comparator_1 (.a(in_1), .b(in_2), .eq(comparator_1_eq), .lt(comparator_1_lt));  // open: gt
  or or_1 (leq_log, comparator_1_eq, comparator_1_lt);
endmodule

module test (
  input  DAT,
  input  CLK,
  input  RESET
);

  wire d_ff_1_q, d_ff_2_q, d_ff_3_q, d_ff_4_q, d_ff_5_q, d_ff_6_q, d_ff_7_q, d_ff_8_q, or_1_out;

  or or_1 (or_1_out, d_ff_8_q, DAT);
  D_Flip_Flop d_ff_1 (.clk(CLK), .D(or_1_out), .Q(d_ff_1_q), .reset(RESET));  // open: Qn, preset
  D_Flip_Flop d_ff_2 (.clk(CLK), .D(d_ff_1_q), .Q(d_ff_2_q), .reset(RESET));  // open: Qn, preset
  D_Flip_Flop d_ff_3 (.clk(CLK), .D(d_ff_2_q), .Q(d_ff_3_q), .reset(RESET));  // open: Qn, preset
  D_Flip_Flop d_ff_4 (.clk(CLK), .D(d_ff_3_q), .Q(d_ff_4_q), .reset(RESET));  // open: Qn, preset
  D_Flip_Flop d_ff_5 (.clk(CLK), .D(d_ff_4_q), .Q(d_ff_5_q), .reset(RESET));  // open: Qn, preset
  D_Flip_Flop d_ff_6 (.clk(CLK), .D(d_ff_5_q), .Q(d_ff_6_q), .reset(RESET));  // open: Qn, preset
  D_Flip_Flop d_ff_7 (.clk(CLK), .D(d_ff_6_q), .Q(d_ff_7_q), .reset(RESET));  // open: Qn, preset
  D_Flip_Flop d_ff_8 (.clk(CLK), .D(d_ff_7_q), .Q(d_ff_8_q), .reset(RESET));  // open: Qn, preset
endmodule

module FSM (
  input  CLK,
  input  RST,
  output RAM_IN_STR,
  output [2:0] stage,
  output RAM__IN_OUT,
  output ABC_REG_EN,
  output A_DAT_EN,
  output B_DAT_EN,
  output nA_B,
  output CNTR_EN,
  output nCNTR_REG,
  output JMP_RDY
);

  Counter #(.max('h7), .width(3)) counter_1 (
    .load(1'b0), .count(1'b1), .Q(stage), .up(1'b1), .clk(CLK), .clr(RST));  // open: D, carry
  PLA #(.in_width(3), .out_width(9), .\table ("000 001000110 # ld C\n001 001000110 # ld C, C>B\n010 001000110 # ld C, C>B, B>A\n011 010001010 # ld Adt\n100 010110010 # ld B dt\n101 010100001 # ld [B] ram\n110 100000000 # subleq ld c\n111 000000000")) pla_1 (
    .in(stage),
    .out({JMP_RDY, nCNTR_REG, CNTR_EN, nA_B, B_DAT_EN, A_DAT_EN, ABC_REG_EN, RAM__IN_OUT, RAM_IN_STR}));
endmodule
